# Fritzing sketch LoopingLouie-pcb (saved by Fritzing 0.9.6b)
breadboards: 1

parts:
  S1 = Square Pushbutton
  M1 = DC Motor
  LED1 = LED - 3mm [color="Red (633nm)" current=0.030 package="3 mm [THT]"]
  LED2 = LED - 3mm [color="Green (565nm)" current=0.030 package="3 mm [THT]"]
  R2 = Resistor [tolerance=±5% resistance=10k package=THT]
  R1 = Resistor [tolerance=±5% resistance=10k package=THT]
  R3 = Rotary Potentiometer (Large) [maximum_resistance=100kΩ package=THT]
  R4 = Resistor [tolerance=±5% resistance=470 power=0.25 package=THT]
  R5 = Resistor [tolerance=±5% power=0.25 resistance=470 package=THT]
  Q1 = MOSFET-NCHANNEL [package=to220v]
  D1 = Diode [package=diode-1n4001]
  WeMos_D1_Mini1 = WeMos D1 Mini
  S2 = Square Pushbutton
  C2 = Film/Foil Capacitor [capacitance=100nF voltage=35V package="5mm [THT, pp]"]
  R6 = Resistor [tolerance=±5% power=0.25 resistance=100k package=THT]
  R7 = Resistor [tolerance=±5% power=0.25 resistance=100 package=THT]

nets:
  N1: S1.leg0, R3.leg2, WeMos_D1_Mini1.3V3, S2.leg0
  N2: S1.leg1, R1.Pin_0
  N3: M1.pin_1, Q1.D, D1.A, C2.+
  N4: M1.pin_2, D1.C, WeMos_D1_Mini1.5V, C2.-
  N5: LED1.cathode, R5.Pin_0
  N6: LED1.anode, WeMos_D1_Mini1.D8
  N7: LED2.cathode, R4.Pin_0
  N8: LED2.anode, WeMos_D1_Mini1.D7
  N9: R2.Pin_0, S2.leg1
  N10: R2.Pin_1, R1.Pin_1, R3.leg1, R4.Pin_1, R5.Pin_1, Q1.S, WeMos_D1_Mini1.D0, WeMos_D1_Mini1.D1, WeMos_D1_Mini1.G, R6.Pin_1
  N11: R3.wiper, WeMos_D1_Mini1.A0
  N12: Q1.G, R6.Pin_0, R7.Pin_0
  N13: WeMos_D1_Mini1.D6, R7.Pin_1
